# Fritzing sketch serial-lcd-buttons-potent (saved by Fritzing 0.9.0b)
breadboards: 1

parts:
  LCD1 = LCD screen
  Part1 = Arduino Uno (Rev3) - ICSP

nets:
  VSS: LCD1.VSS, LCD1.R/W, LCD1.LED-, Part1.GND
  VDD: LCD1.VDD, LCD1.LED+, Part1.5V
  N1: LCD1.RS, Part1.ICSP_MISO, Part1.D12/MISO
  N2: LCD1.E, Part1.ICSP_MOSI, Part1.D11_PWM/MOSI
  N3: LCD1.DB4, Part1.D5_PWM
  N4: LCD1.DB5, Part1.D4
  N5: LCD1.DB6, Part1.D3_PWM
  N6: LCD1.DB7, Part1.D2
